# Fritzing sketch 1130 Uno (saved by Fritzing 0.9.10b)
circuit board: 10cm x 6cm
breadboards: 2

parts:
  Uno = Arduino Uno (Rev3)
  LED1 = smd LED [color="Red (633nm)" package="0603 [SMD]"]
  R1 = Resistor [tolerance=±5% resistance=330 package="0805 [SMD]"]
  Switch_1 = SWITCH_SPDT [package=kps-1290]
  Sensor_1 = DHT22 module

nets (from the schematic view):
  N1: Uno.GND, LED1.anode, Switch_1.S, Sensor_1.-
  N2: Uno.D2, R1.Pin_1
  N3: Uno.D4, Sensor_1.Out
  N4: Uno.D7, Switch_1.O
  N5: Uno.3V3, Switch_1.P, Sensor_1.+
  N6: LED1.cathode, R1.Pin_0

custom parts:
  DHT22 module: DHT22 module. Pins VCC Data GND.
